// Logisim project MIPS-L.circ as structural Verilog: 14 circuits, main circuit DATAPATH
module DATAPATH (
  input  [31:0] DOUT_ROM,
  input  [31:0] DOUT_RAM,
  input  [1:0] SEL_OP1,
  input  SEL_OP2,
  input  WR_ACC,
  input  SEL_ULA,
  input  clock,
  output [5:0] OPCODE,
  output [25:0] ADD_RAM,
  output [31:0] DIN_RAM
);

  wire [31:0] bit_extender_1_out, IR_q, multiplexer_1_out, ULA_ula_output, undriven;

  Multiplexer #(.width(32), .enable("false")) multiplexer_1 (
    .in0(DOUT_RAM), .in1(bit_extender_1_out), .out(multiplexer_1_out), .sel(SEL_OP2));
  Register #(.width(32)) IR (.D(DOUT_ROM), .en(1'b1), .Q(IR_q), .clk(clock), .clr(1'b0));
  IR_bits_distributor ir_bits_distributor_1 (.Input(IR_q), .ADDRESS(ADD_RAM), .OPCODE(OPCODE));
  ULA ULA (.Input_acc(DIN_RAM), .Input_mux(multiplexer_1_out), .SEL_ULA(SEL_ULA), .ULA_Output(ULA_ula_output));
  assign bit_extender_1_out = {{6{1'b0}}, ADD_RAM};  // Bit_Extender bit_extender_1
  Multiplexer #(.select(2), .width(32), .enable("false")) multiplexer_2 (
    .in0(DOUT_RAM), .in1(bit_extender_1_out), .in2(ULA_ula_output), .sel(SEL_OP1));  // open: in3, out
  Register #(.width(32)) ACC (.D(undriven), .en(WR_ACC), .Q(DIN_RAM), .clk(clock), .clr(1'b0));

  // Notes on the sheet:
  //   00 = ULA
  //   01 = ADD_IR
  //   10 = DOUT_RAM
endmodule

module ULA (
  input  [31:0] Input_acc,
  input  [31:0] Input_mux,
  input  SEL_ULA,
  output [31:0] ULA_Output
);

  wire [31:0] adder_1_out, multiplexer_1_out, not_1_out;

  assign not_1_out = ~Input_mux;  // NOT_Gate not_1, 32 bits wide
  Adder #(.width(32)) adder_1 (.a(not_1_out), .b(32'h1), .out(adder_1_out));  // open: cin, cout
  Multiplexer #(.width(32), .enable("false")) multiplexer_1 (
    .in0(Input_mux), .in1(adder_1_out), .out(multiplexer_1_out), .sel(SEL_ULA));
  Adder #(.width(32)) adder_2 (.a(Input_acc), .b(multiplexer_1_out), .out(ULA_Output));  // open: cin, cout
endmodule

// IR_dsitributor
module IR_bits_distributor (
  input  [31:0] Input,
  output [25:0] ADDRESS,
  output [5:0] OPCODE
);


  assign ADDRESS = Input[25:0];
  assign OPCODE = Input[31:26];
endmodule

module CONTROL_EN_RAM (
  input  OP31,
  input  OP30,
  input  OP29,
  input  OP28,
  input  OP27,
  input  OP26,
  output EN_RAM
);

  wire and_1_out, and_2_out, and_3_out, and_4_out, not_1_out, not_2_out, not_3_out, not_4_out, not_5_out,
       not_6_out, not_7_out, not_8_out, not_9_out, not_10_out, not_11_out, not_12_out, not_13_out,
       not_14_out, not_15_out, not_16_out, not_17_out, not_18_out, not_19_out;

  not not_1 (not_1_out, OP27);
  not not_2 (not_2_out, OP28);
  not not_3 (not_3_out, OP29);
  not not_4 (not_4_out, OP30);
  not not_5 (not_5_out, OP31);
  not not_6 (not_6_out, OP26);
  not not_7 (not_7_out, OP28);
  not not_8 (not_8_out, OP29);
  not not_9 (not_9_out, OP30);
  not not_10 (not_10_out, OP31);
  not not_11 (not_11_out, OP26);
  not not_12 (not_12_out, OP27);
  not not_13 (not_13_out, OP29);
  not not_14 (not_14_out, OP30);
  not not_15 (not_15_out, OP31);
  not not_16 (not_16_out, OP26);
  not not_17 (not_17_out, OP29);
  not not_18 (not_18_out, OP30);
  not not_19 (not_19_out, OP31);
  and and_1 (and_1_out, OP26, not_1_out, not_2_out, not_3_out, not_4_out, not_5_out);
  and and_2 (and_2_out, not_6_out, OP27, not_7_out, not_8_out, not_9_out, not_10_out);
  and and_3 (and_3_out, not_11_out, not_12_out, OP28, not_13_out, not_14_out, not_15_out);
  and and_4 (and_4_out, not_16_out, OP27, OP28, not_17_out, not_18_out, not_19_out);
  or or_1 (EN_RAM, and_1_out, and_2_out, and_3_out, and_4_out);
endmodule

module CONTROL_WR_RAM (
  input  OP31,
  input  OP30,
  input  OP29,
  input  OP28,
  input  OP27,
  input  OP26,
  output WR_RAM
);

  wire not_1_out, not_2_out, not_3_out, not_4_out, not_5_out;

  not not_1 (not_1_out, OP27);
  not not_2 (not_2_out, OP28);
  not not_3 (not_3_out, OP29);
  not not_4 (not_4_out, OP30);
  not not_5 (not_5_out, OP31);
  and and_1 (WR_RAM, OP26, not_1_out, not_2_out, not_3_out, not_4_out, not_5_out);
endmodule

module CONTROL_RD_RAM (
  input  OP31,
  input  OP30,
  input  OP29,
  input  OP28,
  input  OP27,
  input  OP26,
  output RD_RAM
);

  wire and_1_out, and_2_out, and_3_out, not_1_out, not_2_out, not_3_out, not_4_out, not_5_out, not_6_out,
       not_7_out, not_8_out, not_9_out, not_10_out, not_11_out, not_12_out, not_13_out, not_14_out;

  not not_1 (not_1_out, OP26);
  not not_2 (not_2_out, OP28);
  not not_3 (not_3_out, OP29);
  not not_4 (not_4_out, OP30);
  not not_5 (not_5_out, OP31);
  not not_6 (not_6_out, OP26);
  not not_7 (not_7_out, OP27);
  not not_8 (not_8_out, OP29);
  not not_9 (not_9_out, OP30);
  not not_10 (not_10_out, OP31);
  not not_11 (not_11_out, OP26);
  not not_12 (not_12_out, OP29);
  not not_13 (not_13_out, OP30);
  not not_14 (not_14_out, OP31);
  and and_1 (and_1_out, not_1_out, OP27, not_2_out, not_3_out, not_4_out, not_5_out);
  and and_2 (and_2_out, not_6_out, not_7_out, OP28, not_8_out, not_9_out, not_10_out);
  and and_3 (and_3_out, not_11_out, OP27, OP28, not_12_out, not_13_out, not_14_out);
  or or_1 (RD_RAM, and_1_out, and_2_out, and_3_out);
endmodule

module CONTROL_WR_ACC (
  input  OP31,
  input  OP30,
  input  OP29,
  input  OP28,
  input  OP27,
  input  OP26,
  output WR_ACC
);

  wire not_1_out, or_1_out, or_2_out;

  not not_1 (not_1_out, OP26);
  or or_1 (or_1_out, OP26, OP27, OP28, OP29, OP30, OP31);
  or or_2 (or_2_out, not_1_out, OP27, OP28, OP29, OP30, OP31);
  and and_1 (WR_ACC, or_1_out, or_2_out);
endmodule

module CONTROL_SEL_OP1 (
  input  OP31,
  input  OP30,
  input  OP29,
  input  OP28,
  input  OP27,
  input  OP26,
  output [1:0] SEL_OP1
);

  wire not_1_out, not_2_out, not_3_out, not_4_out, not_5_out, not_6_out, not_7_out, not_8_out, not_9_out;

  not not_1 (not_1_out, OP26);
  not not_2 (not_2_out, OP28);
  not not_3 (not_3_out, OP29);
  not not_4 (not_4_out, OP30);
  not not_5 (not_5_out, OP31);
  not not_6 (not_6_out, OP28);
  not not_7 (not_7_out, OP29);
  not not_8 (not_8_out, OP30);
  not not_9 (not_9_out, OP31);
  and and_1 (SEL_OP1[1], not_1_out, OP27, not_2_out, not_3_out, not_4_out, not_5_out);
  and and_2 (SEL_OP1[0], OP26, OP27, not_6_out, not_7_out, not_8_out, not_9_out);
endmodule

module CONTROL_SEL_OP2 (
  input  OP31,
  input  OP30,
  input  OP29,
  input  OP28,
  input  OP27,
  input  OP26,
  output SEL_OP2
);

  wire and_1_out, and_2_out, not_1_out, not_2_out, not_3_out, not_4_out, not_5_out, not_6_out, not_7_out,
       not_8_out, not_9_out;

  not not_1 (not_1_out, OP26);
  not not_2 (not_2_out, OP27);
  not not_3 (not_3_out, OP29);
  not not_4 (not_4_out, OP30);
  not not_5 (not_5_out, OP31);
  not not_6 (not_6_out, OP26);
  not not_7 (not_7_out, OP29);
  not not_8 (not_8_out, OP30);
  not not_9 (not_9_out, OP31);
  and and_1 (and_1_out, not_1_out, not_2_out, OP28, not_3_out, not_4_out, not_5_out);
  and and_2 (and_2_out, not_6_out, OP27, OP28, not_7_out, not_8_out, not_9_out);
  or or_1 (SEL_OP2, and_1_out, and_2_out);
endmodule

module CONTROL_SEL_ULA (
  input  OP31,
  input  OP30,
  input  OP29,
  input  OP28,
  input  OP27,
  input  OP26,
  output SEL_ULA
);

  wire and_1_out, and_2_out, not_1_out, not_2_out, not_3_out, not_4_out, not_5_out, not_6_out, not_7_out;

  not not_1 (not_1_out, OP26);
  not not_2 (not_2_out, OP29);
  not not_3 (not_3_out, OP30);
  not not_4 (not_4_out, OP31);
  not not_5 (not_5_out, OP29);
  not not_6 (not_6_out, OP30);
  not not_7 (not_7_out, OP31);
  and and_1 (and_1_out, not_1_out, OP27, OP28, not_2_out, not_3_out, not_4_out);
  and and_2 (and_2_out, OP26, OP27, OP28, not_5_out, not_6_out, not_7_out);
  or or_1 (SEL_ULA, and_1_out, and_2_out);
endmodule

module CONTROL_LOGIC (
  input  [5:0] OPCODE,
  output SEL_ULA,
  output SEL_OP2,
  output [1:0] SEL_OP1,
  output WR_ACC,
  output RD_RAM,
  output WR_RAM,
  output EN_PC,
  output EN_RAM
);

  CONTROL_SEL_ULA control_sel_ula_1 (
    .OP31(OPCODE[5]), .OP30(OPCODE[4]), .OP29(OPCODE[3]), .OP28(OPCODE[2]), .OP27(OPCODE[1]),
    .OP26(OPCODE[0]), .SEL_ULA(SEL_ULA));
  CONTROL_SEL_OP2 control_sel_op2_1 (
    .OP31(OPCODE[5]), .OP30(OPCODE[4]), .OP29(OPCODE[3]), .OP28(OPCODE[2]), .OP27(OPCODE[1]),
    .OP26(OPCODE[0]), .SEL_OP2(SEL_OP2));
  CONTROL_SEL_OP1 control_sel_op1_1 (
    .OP31(OPCODE[5]), .OP30(OPCODE[4]), .OP29(OPCODE[3]), .OP28(OPCODE[2]), .OP27(OPCODE[1]),
    .OP26(OPCODE[0]), .SEL_OP1(SEL_OP1));
  CONTROL_WR_ACC control_wr_acc_1 (
    .OP31(OPCODE[5]), .OP30(OPCODE[4]), .OP29(OPCODE[3]), .OP28(OPCODE[2]), .OP27(OPCODE[1]),
    .OP26(OPCODE[0]), .WR_ACC(WR_ACC));
  CONTROL_RD_RAM control_rd_ram_1 (
    .OP31(OPCODE[5]), .OP30(OPCODE[4]), .OP29(OPCODE[3]), .OP28(OPCODE[2]), .OP27(OPCODE[1]),
    .OP26(OPCODE[0]), .RD_RAM(RD_RAM));
  CONTROL_WR_RAM control_wr_ram_1 (
    .OP31(OPCODE[5]), .OP30(OPCODE[4]), .OP29(OPCODE[3]), .OP28(OPCODE[2]), .OP27(OPCODE[1]),
    .OP26(OPCODE[0]), .WR_RAM(WR_RAM));
  CONTROL_EN_RAM control_en_ram_1 (
    .OP31(OPCODE[5]), .OP30(OPCODE[4]), .OP29(OPCODE[3]), .OP28(OPCODE[2]), .OP27(OPCODE[1]),
    .OP26(OPCODE[0]), .EN_RAM(EN_RAM));

  assign EN_PC = 1'b1;
endmodule

module TOPLEVEL (
  input  CLK
);

  wire CONTROL_en_ram, CONTROL_rd_ram, CONTROL_sel_op2, CONTROL_sel_ula, CONTROL_wr_acc, CONTROL_wr_ram;
  wire [1:0] CONTROL_sel_op1;
  wire [5:0] DATAPATH_opcode;
  wire [23:0] n26_to_24_bits_1_output, n26_to_24_bits_2_output;
  wire [25:0] CONTROL_dout_rom, DATAPATH_add_ram;
  wire [31:0] DATAPATH_din_ram, ram_1_data, rom_1_data;

  DATAPATH DATAPATH (
    .ADD_RAM(DATAPATH_add_ram), .DOUT_RAM(ram_1_data), .SEL_OP1(CONTROL_sel_op1), .SEL_OP2(CONTROL_sel_op2),
    .WR_ACC(CONTROL_wr_acc), .DIN_RAM(DATAPATH_din_ram), .SEL_ULA(CONTROL_sel_ula), .clock(CLK),
    .OPCODE(DATAPATH_opcode), .DOUT_ROM(rom_1_data));
  _26_TO_24_BITS u_26_to_24_bits_1 (.INPUT(DATAPATH_add_ram), .OUTPUT(n26_to_24_bits_1_output));
  CONTROL CONTROL (
    .DOUT_ROM(CONTROL_dout_rom), .SEL_ULA(CONTROL_sel_ula), .SEL_OP2(CONTROL_sel_op2),
    .SEL_OP1(CONTROL_sel_op1), .WR_ACC(CONTROL_wr_acc), .RD_RAM(CONTROL_rd_ram), .WR_RAM(CONTROL_wr_ram),
    .EN_RAM(CONTROL_en_ram), .OPCODE(DATAPATH_opcode), .clk(CLK));
  RAM #(.addrWidth(24), .dataWidth(32), .bus("separate")) ram_1 (
    .addr(n26_to_24_bits_1_output), .din(DATAPATH_din_ram), .data(ram_1_data), .str(CONTROL_wr_ram),
    .sel(CONTROL_en_ram), .clk(CLK), .ld(CONTROL_rd_ram));  // open: clr
  ROM #(.addrWidth(24), .dataWidth(32)) rom_1 (.addr(n26_to_24_bits_2_output), .data(rom_1_data));  // open: sel
  _26_TO_24_BITS u_26_to_24_bits_2 (.INPUT(CONTROL_dout_rom), .OUTPUT(n26_to_24_bits_2_output));
endmodule

module CONTROL (
  input  [5:0] OPCODE,
  input  clk,
  output [25:0] DOUT_ROM,
  output SEL_ULA,
  output SEL_OP2,
  output [1:0] SEL_OP1,
  output WR_ACC,
  output RD_RAM,
  output WR_RAM,
  output EN_RAM
);

  wire control_logic_1_en_pc;
  wire [25:0] adder_1_out;

  CONTROL_LOGIC control_logic_1 (
    .SEL_ULA(SEL_ULA), .SEL_OP2(SEL_OP2), .SEL_OP1(SEL_OP1), .WR_ACC(WR_ACC), .RD_RAM(RD_RAM),
    .WR_RAM(WR_RAM), .EN_PC(control_logic_1_en_pc), .EN_RAM(EN_RAM), .OPCODE(OPCODE));
  Adder #(.width(26)) adder_1 (.a(DOUT_ROM), .b(26'h1), .out(adder_1_out));  // open: cin, cout
  Register #(.width(26)) PC (.D(adder_1_out), .en(control_logic_1_en_pc), .Q(DOUT_ROM), .clk(clk));  // open: clr
endmodule

module _26_TO_24_BITS (
  input  [25:0] INPUT,
  output [23:0] OUTPUT
);


  assign OUTPUT = INPUT[23:0];
endmodule
